# Fritzing sketch routeursolaire (saved by Fritzing 1.0.3b)

parts:
  M1 = ac light dimmer 3terminal
  M2 = ac light dimmer 3terminal
  M3 = ac light dimmer 3terminal
  U1 = ESP32-38PinWide [part_number=ESP32-38PinWide]
  Chauffe_eau = bulb
  M4 = JSY-MK-194T
  Pince_Amperemetrique = JSY-MK-194T sensor2
  OLED_I2C1 = OLED 128x64 I2C Monochrome Display
  YwRobot_Power_Supply1 = YwRobot Breadboard Power Supply [part_number=545043]
  Chauffages_1 = bulb
  Chauffages_2 = bulb
  220V_entrée = 2.1mm Barrel Jack with Terminal Block

nets:
  VCC: M1.VCC, M2.VCC, M3.VCC, U1.3.3, M4.VCC, OLED_I2C1.VDD, YwRobot_Power_Supply1.VCC#5
  GND: M1.GND, M2.GND, M3.GND, U1.GPIO10, U1.GPIO11, M4.GND, OLED_I2C1.GND, YwRobot_Power_Supply1.GND
  N1: M1.PWM, M2.PWM, U1.GPIO26
  N2: M1.OUT, Chauffages_1.2
  N3: M1.N, M2.N, M3.N, Chauffe_eau.1, M4.UN, Chauffages_1.1, Chauffages_2.1, 220V_entrée.POS
  N4: M1.IN, M2.IN, M3.IN, M4.UL, 220V_entrée.NEG
  N5: M2.OUT, Chauffages_2.2
  N6: M3.Z-C, U1.GPIO35
  N7: M3.PWM, U1.GPIO25
  N8: M3.OUT, Chauffe_eau.2
  N9: U1.VIN, YwRobot_Power_Supply1.VCC#9
  N10: U1.GPIO16, M4.TX
  N11: U1.GPIO17, M4.PF, M4.RX
  N12: U1.GPIO21, OLED_I2C1.SDA
  N13: U1.GPIO22, U1.GPIO23, OLED_I2C1.SCK
  N14: M4.JP1-a, Pince_Amperemetrique.Black
  N15: M4.JP1-b, Pince_Amperemetrique.Red

custom parts:
  ac light dimmer 3terminal: ac light dimmer module 3 output terminals.
  ESP32-38PinWide: Generic 38-Pin ESP32 with wide format (only access to one side of pins on a breadboard) based on Stephen Lilley's HiLetgo ESP-WROOM-32 ESP32 ESP-32S Development Board.
  JSY-MK-194T: AC Single Phase Bidirectional Power Energy Meter Module
  JSY-MK-194T sensor2: Sensor 2 for JSY-MK-194T
  YwRobot Breadboard Power Supply: The YwRobot Breadboard Power Supply (MB-V2) has two power rails; they can be 5V or 3V3. Power to the module can be provided through the female USB socket or through the A10 (female) 2.1mm power jack.
